# Fritzing sketch wiring-diagram (saved by Fritzing 0.9.4)
breadboards: 3

parts:
  M1 = DC Motor  # not connected
  M2 = DC Motor  # not connected
  Componente1 = Arduino Uno (Rev3)
  Componente2 = Motor Driver 1A Dual TB6612FNG  # not connected
  LED1 = smd LED [color="Red (633nm)" package="0805 [SMD]"]
  R1 = Resistor [tolerance=±5% resistance=220 package=THT]

nets:
  N1: Componente1.A2, R1.Pin_0
  N2: Componente1.GND, LED1.cathode
  N3: LED1.anode, R1.Pin_1

notes:
  Battery 14.6V
  PS2 Controller
  -------------------
  A1 Acknoledge
  A2 N/A
  A3 Clock
  A4 Attention
  A5 Power 3.3V
  A6 Ground
  A7 N/A
  A8 Command
  A9 Data
  Left motor
  Right motor
  Led Hull MG
